# Fritzing sketch ArduinoNano_GPS (saved by Fritzing 0.9.4)
breadboards: 1

parts:
  Part1 = Arduino Nano (Rev3.0)
  LCD1 = TFT 1.8 inch 160x128 w SD
  Part2 = u-blox NEO-6M GPS Breakout

nets:
  GND: Part1.GND, LCD1.pin2, Part2.GND
  N1: Part1.D3, Part2.TXD
  N2: Part1.D4, Part2.RXD
  N3: Part1.D8, LCD1.pin4
  N4: Part1.D9, Part1.D10, LCD1.pin3, LCD1.pin_5
  N5: Part1.D11/MOSI, LCD1.pin_6
  5V: Part1.5V, LCD1.pin_1, Part2.VCC
  N6: Part1.3V3, LCD1.pin_8
  N7: Part1.D13/SCK, LCD1.pin_7

custom parts:
  TFT 1.8 inch 160x128 w SD: This is a generic 1.8 tft spi lcd display available on ebay and others. The 1.8" display has 128x160 color pixels.
